# Fritzing sketch ifgaccess (saved by Fritzing 0.9.3b)
breadboards: 1

parts:
  Componente1 = Arduino Mega 2560 (Rev3)
  Componente2 = RFID-RC522-v2
  LCD1 = LCD screen
  R1 = Rotary Potentiometer (Small) [maximum_resistance=100kΩ package=THT]
  U2 = ESP8266 WiFi Module [part_number=ESP8266]
  L1 = Solenoid
  Relay_5V1 = Keyes Relay [package=THT]
  VCC1 = Battery block 9V

nets:
  GND: Componente1.GND, Componente2.GND, LCD1.LED-, U2.GND, Relay_5V1.ground
  N1: Componente1.D9_PWM, Componente2.SDA
  N2: Componente1.D8_PWM, Componente2.RST
  3V3: Componente1.3V3, Componente2.3.3V, U2.CH_PD
  N3: Componente1.5V, LCD1.LED+, R1.leg1, R1.leg2, Relay_5V1.signal
  N4: Componente1.D1_TX0, LCD1.RS
  N5: Componente1.D2_PWM, LCD1.E
  N6: Componente1.D4_PWM, LCD1.DB4
  N7: Componente1.D5_PWM, LCD1.DB5
  N8: Componente1.D6_PWM, LCD1.DB6
  N9: Componente1.D7_PWM, LCD1.DB7
  N10: Componente1.D35, U2.RXD
  N11: Componente1.D37, U2.TXD
  N12: Componente1.D38, Relay_5V1.power
  N13: Componente1.D50, Componente2.MISO
  N14: Componente1.D51, Componente2.MOSI
  N15: Componente1.D52, Componente2.SCK
  N16: LCD1.V0, R1.wiper
  N17: L1.pin1, Relay_5V1.NC
  N18: Relay_5V1.C, VCC1.-

custom parts:
  RFID-RC522-v2: A simple China made RFID-RC522 Reader; do check the pin labels, as this is a MFRC522 based clone.
  ESP8266 WiFi Module: Generic WiFi Module based on the ESP8266 with onboard PCB antenna and UART communications
  Keyes Relay: The Keyes 5V relay module is suitable for SCM development, home appliance control. It uses a 5V~12V TIL control signal which can control DC / AC signal.
